# Fritzing sketch EcDownSmsSender (saved by Fritzing 0.9.4)
breadboards: 1

parts:
  LED1 = LED - 5mm [color="Red (633nm)" package="5 mm [THT]"]
  R1 = Resistor [tolerance=±5% resistance=220 package=THT]
  Součástka1 = Arduino Uno (Rev3)
  GSM_SIM_GPSR_SMS_SIM900_SIM1 = SIM800L [package=THT]
  R24 = Resistor [tolerance=±5% resistance=10k package=THT]
  R23 = Photocell (LDR) [package=THT]
  part = Water Level Sensor

nets:
  N1: LED1.cathode, Součástka1.D3_PWM
  N2: LED1.anode, R1.Pin_0
  5V: R1.Pin_1, Součástka1.5V, GSM_SIM_GPSR_SMS_SIM900_SIM1.5V, R23.pin_0, part.VCC
  N3: Součástka1.A0, R24.Pin_1, R23.pin_1
  N4: Součástka1.D10_PWM/SS, GSM_SIM_GPSR_SMS_SIM900_SIM1.SIM_TXD
  N5: Součástka1.D11_PWM/MOSI, GSM_SIM_GPSR_SMS_SIM900_SIM1.SIM_RXD
  GND: Součástka1.GND, GSM_SIM_GPSR_SMS_SIM900_SIM1.GND, R24.Pin_0, part.GND
  N6: Součástka1.D2, part.SIG

custom parts:
  Water Level Sensor: A water level sensor. This sensor operates at 3V to 5V. The Sig (signal) pin outputs an analogue signal that is in proportion to the amount of water in contact with the sensor.

// code stored in the sketch: EcDownSmsSender.ino
int a;
bool running = false;
int LEDpin = 3;


void setup() {
  // put your setup code here, to run once:
  Serial.begin(9600);
  pinMode(LEDpin, OUTPUT);

}

void loop() {
  // put your main code here, to run repeatedly:
  a = analogRead(A0);
  if (a <= 500 && running == false) {
    digitalWrite(LEDpin, HIGH);
    for (int i = 1; i < 20; i++) {
      Serial.println("POslat SMS");
      running = true;
      break;
    }
  } else if (a > 500 && running) {
    delay(100);
    running = false;
    digitalWrite(LEDpin, LOW);

  }
  Serial.println(a);
}
